// Logisim project ALU Circuit.circ as structural Verilog: 8 circuits, main circuit main
module main (
  input  [3:0] S,
  input  ENB,
  input  [2:0] A,
  input  [2:0] B,
  output EQ,
  output LT,
  output GT,
  output [2:0] Out,
  output out_9
);

  wire and_1_out, and_2_out, and_3_out, and_4_out, arithmitic_unit_1_c, compare_unit_2_eq, compare_unit_2_gt,
       compare_unit_2_lt;
  wire [1:0] controlled_buffer_1_out, controlled_buffer_1_out_2;
  wire [2:0] arithmitic_unit_1_out, logic_unit_1_out_6, merger_unit_1_out, shifting_unit_1_out;

  Compare_Unit compare_unit_1 (.A(A), .B(B), .ENB(ENB), .EQ(EQ), .LT(LT), .GT(GT));
  assign {controlled_buffer_1_out_2, controlled_buffer_1_out} = ENB ? S : 4'bz;  // Controlled_Buffer controlled_buffer_1
  and and_1 (and_1_out, controlled_buffer_1_out_2[1], controlled_buffer_1_out_2[0]);
  and and_2 (and_2_out, ~controlled_buffer_1_out_2[0], ~controlled_buffer_1_out_2[1]);  // AND_Gate
  and and_3 (and_3_out, controlled_buffer_1_out_2[1], ~controlled_buffer_1_out_2[0]);  // AND_Gate
  and and_4 (and_4_out, ~controlled_buffer_1_out_2[1], controlled_buffer_1_out_2[0]);  // AND_Gate
  Compare_Unit compare_unit_2 (
    .A(A), .B(B), .ENB(and_4_out), .EQ(compare_unit_2_eq), .LT(compare_unit_2_lt), .GT(compare_unit_2_gt));
  Arithmitic_Unit arithmitic_unit_1 (
    .A(A), .B(B), .S0(controlled_buffer_1_out[0]), .S1(controlled_buffer_1_out[1]), .ENB(and_2_out),
    .Out(arithmitic_unit_1_out), .C(arithmitic_unit_1_c));
  Logic_Unit logic_unit_1 (
    .A(A), .S0(controlled_buffer_1_out[0]), .S1(controlled_buffer_1_out[1]), .B(B), .ENB(and_3_out),
    .out_6(logic_unit_1_out_6));
  Shifting_Unit shifting_unit_1 (
    .S0(controlled_buffer_1_out[0]), .A(A), .ENB(and_1_out), .B(B), .Out(shifting_unit_1_out));
  Multiplexer multiplexer_1 (.in0(1'b0), .in1(arithmitic_unit_1_c), .out(out_9), .sel(and_2_out), .en(ENB));
  Merger_Unit merger_unit_1 (
    .A0(compare_unit_2_eq), .A1(compare_unit_2_lt), .A2(compare_unit_2_gt), .ENB(and_4_out),
    .Out(merger_unit_1_out));
  Multiplexer #(.select(2), .width(3)) multiplexer_2 (
    .in0(arithmitic_unit_1_out), .in1(merger_unit_1_out), .in2(logic_unit_1_out_6),
    .in3(shifting_unit_1_out), .out(Out), .sel(controlled_buffer_1_out_2), .en(ENB));
endmodule

module Arithmitic_Unit (
  input  [2:0] A,
  input  [2:0] B,
  input  S0,
  input  S1,
  input  ENB,
  output [2:0] Out,
  output C
);

  wire ripple_adder_1_cout;
  wire [2:0] multiplexer_1_out, multiplexer_2_out, not_1_out;

  Multiplexer #(.width(3)) multiplexer_1 (.in0(A), .in1(not_1_out), .out(multiplexer_1_out), .sel(S0), .en(ENB));
  assign not_1_out = ~A;  // NOT_Gate not_1, 3 bits wide
  Multiplexer #(.width(3)) multiplexer_2 (.in0(B), .in1(3'b000), .out(multiplexer_2_out), .sel(S1), .en(ENB));
  Ripple_Adder ripple_adder_1 (
    .A(multiplexer_1_out), .B(multiplexer_2_out), .Cin(S0), .ENB(ENB), .Sum(Out), .Cout(ripple_adder_1_cout));
  xor xor_1 (C, S0, ripple_adder_1_cout);
endmodule

module Compare_Unit (
  input  [2:0] A,
  input  [2:0] B,
  input  ENB,
  output EQ,
  output LT,
  output GT
);

  wire and_1_out, and_2_out, and_3_out, and_4_out, and_5_out, xnor_1_out, xnor_2_out, xnor_3_out;
  wire [2:0] controlled_buffer_1_out, controlled_buffer_2_out;

  assign controlled_buffer_1_out = ENB ? A : 3'bz;  // Controlled_Buffer controlled_buffer_1
  assign controlled_buffer_2_out = ENB ? B : 3'bz;  // Controlled_Buffer controlled_buffer_2
  xnor xnor_1 (xnor_1_out, controlled_buffer_1_out[2], controlled_buffer_2_out[2]);
  xnor xnor_2 (xnor_2_out, controlled_buffer_1_out[1], controlled_buffer_2_out[1]);
  xnor xnor_3 (xnor_3_out, controlled_buffer_1_out[0], controlled_buffer_2_out[0]);
  and and_1 (and_1_out, ~controlled_buffer_2_out[0], controlled_buffer_1_out[0]);  // AND_Gate
  and and_2 (and_2_out, ~controlled_buffer_2_out[1], controlled_buffer_1_out[1]);  // AND_Gate
  and and_3 (and_3_out, xnor_2_out, xnor_1_out, and_1_out);
  and and_4 (and_4_out, xnor_1_out, and_2_out);
  and and_5 (and_5_out, ~controlled_buffer_2_out[2], controlled_buffer_1_out[2]);  // AND_Gate
  and and_6 (EQ, xnor_1_out, xnor_2_out, xnor_3_out);
  or or_1 (GT, and_3_out, and_4_out, and_5_out);
  nor nor_1 (LT, EQ, GT);
endmodule

module Logic_Unit (
  input  [2:0] A,
  input  S0,
  input  S1,
  input  [2:0] B,
  input  ENB,
  output [2:0] out_6
);

  wire and_1_out, and_2_out, and_3_out, and_4_out, and_5_out, and_6_out, and_7_out, not_1_out, not_2_out,
       not_3_out, or_1_out, or_2_out, or_3_out, xor_1_out, xor_2_out, xor_3_out;
  wire [1:0] bit_extender_1_out, bit_extender_2_out, or_4_out, shifter_1_out;
  wire [2:0] merger_unit_1_out, merger_unit_2_out, merger_unit_3_out, merger_unit_4_out;

  and and_1 (and_1_out, ENB, S1, S0);
  and and_2 (and_2_out, A[0], B[0]);
  and and_3 (and_3_out, A[1], B[1]);
  and and_4 (and_4_out, A[2], B[2]);
  xor xor_1 (xor_1_out, A[0], B[0]);
  xor xor_2 (xor_2_out, A[1], B[1]);
  xor xor_3 (xor_3_out, A[2], B[2]);
  not not_1 (not_1_out, B[0]);
  not not_2 (not_2_out, B[1]);
  not not_3 (not_3_out, B[2]);
  and and_5 (and_5_out, ~S0, ~S1, ENB);  // AND_Gate
  and and_6 (and_6_out, S0, ~S1, ENB);  // AND_Gate
  or or_1 (or_1_out, A[0], B[0]);
  or or_2 (or_2_out, A[1], B[1]);
  or or_3 (or_3_out, A[2], B[2]);
  and and_7 (and_7_out, ~S0, S1, ENB);  // AND_Gate
  Merger_Unit merger_unit_1 (.A0(xor_1_out), .A1(xor_2_out), .A2(xor_3_out), .ENB(and_6_out), .Out(merger_unit_1_out));
  Merger_Unit merger_unit_2 (.A0(not_1_out), .A1(not_2_out), .A2(not_3_out), .ENB(and_1_out), .Out(merger_unit_2_out));
  Merger_Unit merger_unit_3 (.A0(and_2_out), .A1(and_3_out), .A2(and_4_out), .ENB(and_5_out), .Out(merger_unit_3_out));
  Merger_Unit merger_unit_4 (.A0(or_1_out), .A1(or_2_out), .A2(or_3_out), .ENB(and_7_out), .Out(merger_unit_4_out));
  Multiplexer #(.select(2), .width(3)) multiplexer_1 (
    .in0(merger_unit_3_out), .in1(merger_unit_1_out), .in2(merger_unit_4_out), .in3(merger_unit_2_out),
    .out(out_6), .sel(or_4_out), .en(ENB));
  assign bit_extender_1_out = {{1{1'b0}}, S1};  // Bit_Extender bit_extender_1
  assign bit_extender_2_out = {{1{1'b0}}, S0};  // Bit_Extender bit_extender_2
  Shifter #(.width(2), .shift("rl")) shifter_1 (.in(bit_extender_1_out), .\dist (1'b1), .out(shifter_1_out));
  assign or_4_out = shifter_1_out | bit_extender_2_out;  // OR_Gate or_4, 2 bits wide
endmodule

module Merger_Unit (
  input  A0,
  input  ENB,
  input  A1,
  input  A2,
  output [2:0] Out
);

  wire controlled_buffer_1_out, controlled_buffer_2_out, controlled_buffer_3_out;
  wire [1:0] bit_extender_3_out, not_1_out;
  wire [2:0] bit_extender_1_out, bit_extender_2_out, bit_extender_4_out, shifter_1_out, shifter_2_out,
       shifter_3_out;

  assign controlled_buffer_1_out = ENB ? A0 : 1'bz;  // Controlled_Buffer controlled_buffer_1
  assign controlled_buffer_2_out = ENB ? A1 : 1'bz;  // Controlled_Buffer controlled_buffer_2
  assign controlled_buffer_3_out = ENB ? A2 : 1'bz;  // Controlled_Buffer controlled_buffer_3
  assign bit_extender_1_out = {{2{1'b0}}, controlled_buffer_1_out};  // Bit_Extender bit_extender_1
  assign bit_extender_2_out = {{2{1'b0}}, controlled_buffer_2_out};  // Bit_Extender bit_extender_2
  assign bit_extender_3_out = {{1{1'b0}}, 1'b1};  // Bit_Extender bit_extender_3
  assign bit_extender_4_out = {{2{1'b0}}, controlled_buffer_3_out};  // Bit_Extender bit_extender_4
  Shifter #(.width(3)) shifter_1 (.in(bit_extender_1_out), .\dist (2'b00), .out(shifter_1_out));
  Shifter #(.width(3)) shifter_2 (.in(bit_extender_2_out), .\dist (bit_extender_3_out), .out(shifter_2_out));
  Shifter #(.width(3)) shifter_3 (.in(bit_extender_4_out), .\dist (not_1_out), .out(shifter_3_out));
  assign not_1_out = ~bit_extender_3_out;  // NOT_Gate not_1, 2 bits wide
  assign Out = shifter_1_out | shifter_2_out | shifter_3_out;  // OR_Gate or_1, 3 bits wide
endmodule

module Shifting_Unit (
  input  S0,
  input  [2:0] B,
  input  [2:0] A,
  input  ENB,
  output [2:0] Out
);

  wire multiplexer_1_out, multiplexer_2_out, multiplexer_3_out, multiplexer_4_out, multiplexer_5_out,
       multiplexer_6_out, not_1_out;
  wire [2:0] merger_unit_1_out, merger_unit_2_out;

  Multiplexer #(.select(2)) multiplexer_1 (
    .in0(A[2]), .in1(A[1]), .in2(A[0]), .in3(1'b0), .out(multiplexer_1_out), .sel(B[1:0]), .en(ENB));
  Multiplexer #(.select(2)) multiplexer_2 (
    .in0(A[1]), .in1(A[0]), .in2(1'b0), .in3(1'b0), .out(multiplexer_2_out), .sel(B[1:0]), .en(ENB));
  Multiplexer #(.select(2)) multiplexer_3 (
    .in0(A[0]), .in1(1'b0), .in2(1'b0), .in3(1'b0), .out(multiplexer_3_out), .sel(B[1:0]), .en(ENB));
  Multiplexer #(.select(2)) multiplexer_4 (
    .in0(A[0]), .in1(A[1]), .in2(A[2]), .in3(1'b0), .out(multiplexer_4_out), .sel(B[1:0]), .en(ENB));
  Multiplexer #(.select(2)) multiplexer_5 (
    .in0(A[1]), .in1(A[2]), .in2(1'b0), .in3(1'b0), .out(multiplexer_5_out), .sel(B[1:0]), .en(ENB));
  Multiplexer #(.select(2)) multiplexer_6 (
    .in0(A[2]), .in1(1'b0), .in2(1'b0), .in3(1'b0), .out(multiplexer_6_out), .sel(B[1:0]), .en(ENB));
  not not_1 (not_1_out, S0);
  Merger_Unit merger_unit_1 (
    .A0(multiplexer_3_out), .A1(multiplexer_2_out), .A2(multiplexer_1_out), .ENB(not_1_out),
    .Out(merger_unit_1_out));
  Merger_Unit merger_unit_2 (
    .A0(multiplexer_4_out), .A1(multiplexer_5_out), .A2(multiplexer_6_out), .ENB(S0), .Out(merger_unit_2_out));
  Multiplexer #(.width(3)) multiplexer_7 (
    .in0(merger_unit_1_out), .in1(merger_unit_2_out), .out(Out), .sel(S0), .en(ENB));
endmodule

module Ripple_Adder (
  input  [2:0] A,
  input  [2:0] B,
  input  Cin,
  input  ENB,
  output [2:0] Sum,
  output Cout
);

  wire full_adder_1_cout, full_adder_1_sum, full_adder_2_cout, full_adder_2_sum, full_adder_3_sum;
  wire [2:0] controlled_buffer_1_out, controlled_buffer_2_out;

  assign controlled_buffer_1_out = ENB ? A : 3'bz;  // Controlled_Buffer controlled_buffer_1
  assign controlled_buffer_2_out = ENB ? B : 3'bz;  // Controlled_Buffer controlled_buffer_2
  Full_Adder full_adder_1 (
    .X(controlled_buffer_1_out[0]), .Y(controlled_buffer_2_out[0]), .Cin(Cin), .ENB(ENB),
    .Sum(full_adder_1_sum), .Cout(full_adder_1_cout));
  Full_Adder full_adder_2 (
    .X(controlled_buffer_1_out[1]), .Y(controlled_buffer_2_out[1]), .Cin(full_adder_1_cout), .ENB(ENB),
    .Sum(full_adder_2_sum), .Cout(full_adder_2_cout));
  Full_Adder full_adder_3 (
    .X(controlled_buffer_1_out[2]), .Y(controlled_buffer_2_out[2]), .Cin(full_adder_2_cout), .ENB(ENB),
    .Sum(full_adder_3_sum), .Cout(Cout));
  Merger_Unit merger_unit_1 (.A0(full_adder_1_sum), .A1(full_adder_2_sum), .A2(full_adder_3_sum), .ENB(ENB), .Out(Sum));
endmodule

module Full_Adder (
  input  X,
  input  Y,
  input  Cin,
  input  ENB,
  output Sum,
  output Cout
);

  wire and_1_out, and_2_out, and_3_out, controlled_buffer_1_out, controlled_buffer_2_out,
       controlled_buffer_3_out;

  assign controlled_buffer_1_out = ENB ? X : 1'bz;  // Controlled_Buffer controlled_buffer_1
  assign controlled_buffer_2_out = ENB ? Y : 1'bz;  // Controlled_Buffer controlled_buffer_2
  assign controlled_buffer_3_out = ENB ? Cin : 1'bz;  // Controlled_Buffer controlled_buffer_3
  ExactlyOne xor_1 (
    .out(Sum), .in0(controlled_buffer_1_out), .in1(controlled_buffer_2_out), .in2(controlled_buffer_3_out));
  and and_1 (and_1_out, controlled_buffer_3_out, controlled_buffer_3_out);
  and and_2 (and_2_out, controlled_buffer_3_out, controlled_buffer_1_out);
  and and_3 (and_3_out, controlled_buffer_1_out, controlled_buffer_2_out);
  or or_1 (Cout, and_1_out, and_2_out, and_3_out);
endmodule
